# Fritzing sketch proiect_pmp (saved by Fritzing 0.9.3b)
breadboards: 1

parts:
  J1 = Basic Servo
  Part1 = Arduino Uno (Rev3)
  Part3 = Bluetooth HC-05 Macho
  HC-SR04_Sensor_1 = HC-SR04 Ultrasonic Distance Sensor
  J2 = Piezo Speaker
  M1 = DC Motor
  M2 = DC Motor
  S1 = H-Bridge with L298N
  U1 = WS2812 RGB LED matrix 1x8
  U2 = WS2812 RGB LED matrix 1x8

nets:
  GND: J1.gnd, Part1.GND, Part3.GND, HC-SR04_Sensor_1.GND, J2.pin1, S1.GND, U1.GND#0
  VCC: J1.vcc, Part1.5V, Part3.VCC, HC-SR04_Sensor_1.VCC, S1.5V, U1.VCC#1
  N1: J1.pulse, Part1.D4
  N2: Part1.D9_PWM, HC-SR04_Sensor_1.TRIG
  N3: Part1.D10_PWM/SS, HC-SR04_Sensor_1.ECHO
  N4: Part1.D11_PWM/MOSI, S1.IN3
  N5: Part1.D0/RX, Part3.TXD
  N6: Part1.D1/TX, Part3.RXD
  N7: Part1.D2, J2.pin2
  N8: Part1.D3_PWM, S1.IN4
  N9: Part1.D5_PWM, S1.IN2
  N10: Part1.D6_PWM, S1.IN1
  N11: Part1.D7, U1.DIN
  VIN: Part1.VIN, S1.12V
  N12: M1.pin_1, S1.M2-02
  N13: M1.pin_2, S1.M2-01
  N14: M2.pin_1, S1.M1-02
  N15: M2.pin_2, S1.M1-01
  N16: U1.GND#4, U1.GND#7, U2.GND
  N17: U1.VCC#5, U2.VCC
  N18: U1.DOUT, U2.DIN

custom parts:
  H-Bridge with L298N: h-bridge
  WS2812 RGB LED matrix 1x8: WS2812 matrix 1x8
